# Fritzing sketch ders2 (saved by Fritzing 0.9.10b)
breadboards: 1

parts:
  Parça1 = Arduino Uno (Rev3)
  R1 = Resistor [tolerance=±5% power=0.25 resistance=220 package=THT]
  LED1 = LED - 5mm [color="Red (633nm)" current=0.030 package="5 mm [THT]"]

nets:
  N1: Parça1.D13/SCK, R1.Pin_1
  N2: Parça1.GND, LED1.cathode
  N3: R1.Pin_0, LED1.anode
