# Fritzing sketch ders6 (saved by Fritzing 0.9.10b)
breadboards: 1

parts:
  Parça1 = Arduino Uno (Rev3)
  R1 = Rotary Potentiometer (Small) [maximum_resistance=100kΩ knob_status=50% power=0.5W package=THT]
  LED1 = LED - 5mm [color="Red (633nm)" current=0.030 package="5 mm [THT]"]
  LED2 = LED - 5mm [color="Red (633nm)" current=0.030 package="5 mm [THT]"]
  LED3 = LED - 5mm [color="Red (633nm)" current=0.030 package="5 mm [THT]"]
  R2 = Resistor [tolerance=±5% power=0.25 resistance=220 package=THT]
  R5 = Resistor [tolerance=±5% power=0.25 resistance=220 package=THT]
  R6 = Resistor [tolerance=±5% power=0.25 resistance=220 package=THT]

nets:
  N1: Parça1.A0, R1.wiper
  N2: Parça1.D2, R2.Pin_1
  N3: Parça1.D4, R5.Pin_1
  N4: Parça1.D6_PWM, R6.Pin_1
  N5: Parça1.5V, R1.leg2
  N6: Parça1.GND, R1.leg1, LED1.cathode, LED2.cathode, LED3.cathode
  N7: LED1.anode, R2.Pin_0
  N8: LED2.anode, R5.Pin_0
  N9: LED3.anode, R6.Pin_0
