# Fritzing sketch Untitled Sketch 2 (saved by Fritzing 0.9.10b)
breadboards: 1

parts:
  Parça1 = Arduino Uno (Rev3)
  J1 = Piezo Speaker
  R1 = Resistor [tolerance=±20% power=0.25 resistance=100 package=THT]

nets:
  N1: Parça1.D9_PWM, R1.Pin_1
  N2: Parça1.GND, J1.pin1
  N3: J1.pin2, R1.Pin_0
