# Fritzing sketch der8 (saved by Fritzing 0.9.10b)
breadboards: 1

parts:
  Parça1 = Arduino Uno (Rev3)
  R1 = Resistor [tolerance=±5% power=0.25 resistance=220 package=THT]
  R2 = Photocell (LDR) [package=THT]

nets:
  N1: Parça1.A5/SCL, R1.Pin_1, R2.pin_0
  N2: Parça1.5V, R2.pin_1
  N3: Parça1.GND, R1.Pin_0
