# Fritzing sketch devre (saved by Fritzing 0.9.10b)
breadboards: 1

parts:
  Parça1 = SRF05 Ultrasonic Rangefinder
  Parça2 = Arduino Uno (Rev3)

nets:
  VCC: Parça1.VCC, Parça2.5V
  N1: Parça1.Trig, Parça2.D3_PWM
  N2: Parça1.Echo, Parça2.D2
  GND: Parça1.GND, Parça2.GND
