# Fritzing sketch Untitled Sketch (saved by Fritzing 0.9.10b)

parts:
  Parça1 = Arduino Uno (Rev3)
  Parça2 = Black Joystick KY-023

nets:
  N1: Parça1.A4/SDA, Parça2.VRy
  N2: Parça1.A5/SCL, Parça2.VRx
  N3: Parça1.D2, Parça2.SW
  5V: Parça1.5V, Parça2.+5V
  GND: Parça1.GND, Parça2.GND

custom parts:
  Black Joystick KY-023: Description: The joystick is a combination of 2 analoog potentiometer and a digital switch. Arduino GND --> Module pin - Arduino +5V --> Module pin +5V Arduino Analoog 0 --> Module VRx Arduino Analoog 1 --> Module VRy Arduino Digital --> Module SW Dimensions: 1" x 1.25"
