# Fritzing sketch Untitled Sketch (saved by Fritzing 0.9.10b)

parts:
  SERVO1 = Tower Pro SG90 servo [part_number=101246]
  Parça1 = Arduino Uno (Rev3)

nets:
  N1: SERVO1.Signal, Parça1.D2
  +5V: SERVO1.+5V, Parça1.5V
  GND: SERVO1.GND, Parça1.GND

custom parts:
  Tower Pro SG90 servo: Original file by John De Cristofaro http://www.adafruit.com/products/1449 Adafruit Feedback Servo (Small) Edited by: e-radionica.com 28/9/2015
