# Fritzing sketch ders (saved by Fritzing 0.9.10b)

parts:
  Parça1 = Arduino Uno (Rev3)
  Mod1 = KY-016 RGB Full Color LED Module [package="Breakout board"]

nets:
  N1: Parça1.D9_PWM, Mod1.B
  N2: Parça1.D10_PWM/SS, Mod1.G
  N3: Parça1.D11_PWM/MOSI, Mod1.R
  N4: Parça1.GND, Mod1.-

custom parts:
  KY-016 RGB Full Color LED Module: KY-016 Arduino full color 5mm RGB LED, different colors can be obtained by mixing the three primary colors.
