# Fritzing sketch devre (saved by Fritzing 0.9.10b)
breadboards: 1

parts:
  Parça1 = SRF05 Ultrasonic Rangefinder
  Parça2 = Arduino Uno (Rev3)
  J1 = Piezo Speaker
  R1 = Resistor [tolerance=±5% power=0.25 resistance=100 package=THT]

nets:
  VCC: Parça1.VCC, Parça2.5V
  N1: Parça1.Trig, Parça2.D3_PWM
  N2: Parça1.Echo, Parça2.D2
  GND: Parça1.GND, Parça2.GND, J1.pin1
  N3: Parça2.D11_PWM/MOSI, R1.Pin_1
  N4: J1.pin2, R1.Pin_0
