# Fritzing sketch ders9 (saved by Fritzing 0.9.10b)
breadboards: 1

parts:
  Parça1 = Arduino Uno (Rev3)
  R1 = Resistor [tolerance=±5% power=0.25 resistance=220 package=THT]
  R2 = Photocell (LDR) [package=THT]
  LED1 = LED - 5mm [color="Red (633nm)" current=0.030 package="5 mm [THT]"]
  R3 = Resistor [tolerance=±5% power=0.25 resistance=220 package=THT]

nets:
  N1: Parça1.A5/SCL, R1.Pin_1, R2.pin_0
  N2: Parça1.D12/MISO, R3.Pin_1
  N3: Parça1.5V, R2.pin_1
  N4: Parça1.GND, R1.Pin_0, LED1.cathode
  N5: LED1.anode, R3.Pin_0
